// Logisim project cr8.circ as structural Verilog: 10 circuits, main circuit dflop
module main (
);

  wire ALU_SEL_A, ALU_SEL_B, ALU_SEL_C, ALU_SEL_D, ALU_SEL_F, ALU_SEL_K, ALU_SEL_X, ALU_SEL_Y, ALU_SEL_Z,
       and_1_out, AR_PC, AR_SP, AW_LR, AW_PC, AW_SP, AW_XY, CLK, demultiplexer_4_out7, DR_A, DR_B, DR_C,
       DR_D, DR_F, DR_K, DR_X, DR_Y, DR_Z, DW_A, DW_AF, DW_ALU, DW_B, DW_C, DW_D, DW_F, DW_IMM, DW_IO, DW_K,
       DW_MEM, DW_RHS, DW_X, DW_Y, DW_Z, not_1_out, not_2_out, or_2_out, or_3_out, or_5_out;
  wire [3:0] DR, DW, multiplexer_1_out;
  wire [7:0] A_q, alu_1_f, alu_1_q, ALUB, B_q, C_q, controlled_buffer_9_out, D_q, DB, F_q, IO_q, K_q,
       mem_1_d_out, multiplexer_2_out, multiplexer_3_out, X_q, Y_q, Z_q;
  wire [7:4] LHS_q, RHS_q;
  wire [9:0] SP_q;
  wire [15:0] AB, PC_q;

  Clock clock_1 (.out(CLK));
  Demultiplexer #(.select(4)) demultiplexer_1 (
    .out0(ALU_SEL_A), .out1(ALU_SEL_B), .out2(ALU_SEL_C), .out3(ALU_SEL_D), .out4(ALU_SEL_X),
    .out5(ALU_SEL_Y), .out6(ALU_SEL_Z), .out7(ALU_SEL_F), .out8(ALU_SEL_K), .in(1'b1), .sel(DR));  // open: out9, out10, out11, out12, out13, out14, out15
  Demultiplexer #(.select(2)) demultiplexer_2 (
    .out0(AW_PC), .out1(AW_SP), .out2(AW_XY), .out3(AW_LR), .in(1'b1), .sel(2'b10));
  Demultiplexer #(.select(4)) demultiplexer_3 (
    .out0(DW_A), .out1(DW_B), .out2(DW_C), .out3(DW_D), .out4(DW_X), .out5(DW_Y), .out6(DW_Z), .out7(DW_F),
    .out8(DW_K), .out9(DW_AF), .out10(DW_ALU), .out11(DW_MEM), .out12(DW_IO), .out13(DW_IMM), .out14(DW_RHS),
    .in(1'b1), .sel(multiplexer_1_out));  // open: out15
  Multiplexer #(.width(4)) multiplexer_1 (.in0(4'b1001), .in1(DW), .out(multiplexer_1_out));  // open: sel
  Demultiplexer #(.select(4)) demultiplexer_4 (
    .out0(DR_A), .out1(DR_B), .out2(DR_C), .out3(DR_D), .out4(DR_X), .out5(DR_Y), .out6(DR_Z),
    .out7(demultiplexer_4_out7), .out8(DR_K), .in(1'b0), .sel(DR));  // open: out9, out10, out11, out12, out13, out14, out15
  assign DB = DW_IMM ? 8'h3 : 8'bz;  // Controlled_Buffer controlled_buffer_1
  or or_1 (DR_F, demultiplexer_4_out7, 1'b0);
  _7_Segment_Display u_7_segment_display_1 ();  // open: g, f, a, b, e, d, c, dp
  // BCD_to_7_Segment_decoder bcd_to_7_segment_decoder_1: pin names not known
  // Binary_to_BCD_converter #(.binvalue(8)) binary_to_bcd_converter_1: pin names not known; wires that end beside it: DB
  Multiplexer #(.width(8)) multiplexer_2 (.in0(DB), .in1({4'b0000, DB[3:0]}), .out(multiplexer_2_out));  // open: sel
  or or_2 (or_2_out, 1'b0, 1'b0);
  _7_Segment_Display u_7_segment_display_2 ();  // open: g, f, a, b, e, d, c, dp
  _7_Segment_Display u_7_segment_display_3 ();  // open: g, f, a, b, e, d, c, dp
  // BCD_to_7_Segment_decoder bcd_to_7_segment_decoder_2: pin names not known
  // BCD_to_7_Segment_decoder bcd_to_7_segment_decoder_3: pin names not known
  assign DB = DW_F ? F_q : 8'bz;  // Controlled_Buffer controlled_buffer_2
  vis_register F (.RE(DR_F), .CLK(CLK), .BUS_IN(DB), .RST(1'b0), .Q(F_q));
  assign DB = DW_IO ? IO_q : 8'bz;  // Controlled_Buffer controlled_buffer_3
  vis_register IO (.RE(1'b0), .CLK(CLK), .BUS_IN(DB), .RST(1'b0), .Q(IO_q));
  assign DB = DW_A ? A_q : 8'bz;  // Controlled_Buffer controlled_buffer_4
  vis_register A (.RE(DR_A), .CLK(CLK), .BUS_IN(DB), .RST(1'b0), .Q(A_q));
  Controlled_Buffer #(.width(8)) controlled_buffer_5 (.in(A_q), .en(ALU_SEL_A));  // open: out
  assign DB = DW_K ? K_q : 8'bz;  // Controlled_Buffer controlled_buffer_6
  vis_register K (.RE(DR_K), .CLK(CLK), .BUS_IN(DB), .RST(1'b0), .Q(K_q));
  Controlled_Buffer #(.width(8)) controlled_buffer_7 (.in(K_q), .en(ALU_SEL_K));  // open: out
  vis_register LHS (.RE(or_2_out), .CLK(CLK), .BUS_IN(multiplexer_2_out), .RST(1'b0), .Q({LHS_q, DR}));
  Hex_Digit_Display #(.decimalPoint("false")) hex_digit_display_1 (.value(AB[15:12]));
  Multiplexer #(.width(8)) multiplexer_3 (.in0(DB), .in1({4'b0000, DB[7:4]}), .out(multiplexer_3_out));  // open: sel
  or or_3 (or_3_out, 1'b0, 1'b0);
  assign DB = DW_ALU ? alu_1_q : 8'bz;  // Controlled_Buffer controlled_buffer_8
  assign controlled_buffer_9_out = 1'b0 ? DB : 8'bz;  // Controlled_Buffer controlled_buffer_9
  Hex_Digit_Display #(.decimalPoint("false")) hex_digit_display_2 (.value(AB[11:8]));
  Hex_Digit_Display #(.decimalPoint("false")) hex_digit_display_3 (.value(AB[7:4]));
  alu alu_1 (.A(ALUB), .B({RHS_q, DW}), .OP(3'b101), .F_in(F_q), .F(alu_1_f), .Q(alu_1_q));
  Hex_Digit_Display #(.decimalPoint("false")) hex_digit_display_4 (.value(AB[3:0]));
  assign DB = DW_B ? B_q : 8'bz;  // Controlled_Buffer controlled_buffer_10
  vis_register B (.RE(DR_B), .CLK(CLK), .BUS_IN(DB), .RST(1'b0), .Q(B_q));
  assign ALUB = ALU_SEL_B ? B_q : 8'bz;  // Controlled_Buffer controlled_buffer_11
  assign DB = DW_X ? X_q : 8'bz;  // Controlled_Buffer controlled_buffer_12
  vis_register X (.RE(DR_X), .CLK(CLK), .BUS_IN(DB), .RST(1'b0), .Q(X_q));
  vis_register RHS (.RE(or_3_out), .CLK(CLK), .BUS_IN(multiplexer_3_out), .RST(1'b0), .Q({RHS_q, DW}));
  assign DB = DW_AF ? alu_1_f : 8'bz;  // Controlled_Buffer controlled_buffer_13
  not not_1 (not_1_out, alu_1_f[4]);
  and and_1 (and_1_out, not_1_out, 1'b0);
  or or_4 (AR_PC, and_1_out, 1'b0);
  assign ALUB = ALU_SEL_X ? X_q : 8'bz;  // Controlled_Buffer controlled_buffer_14
  assign AB = AW_XY ? {Y_q, X_q} : 16'bz;  // Controlled_Buffer controlled_buffer_15
  assign DB = DW_RHS ? {RHS_q, DW} : 8'bz;  // Controlled_Buffer controlled_buffer_16
  assign AB = AW_LR ? {RHS_q, DW, LHS_q, DR} : 16'bz;  // Controlled_Buffer controlled_buffer_17
  assign DB = DW_MEM ? mem_1_d_out : 8'bz;  // Controlled_Buffer controlled_buffer_18
  mem mem_1 (.ADDR(AB), .WE(1'b0), .CLK(CLK), .D_in(controlled_buffer_9_out), .D_Out(mem_1_d_out));
  Counter #(.max('hffff), .width(16)) PC (
    .clr(1'b0), .load(AR_PC), .up(1'b1), .count(1'b0), .clk(CLK), .D(AB), .Q(PC_q));  // open: carry
  vis_register C (.RE(DR_C), .CLK(CLK), .BUS_IN(DB), .RST(1'b0), .Q(C_q));
  assign DB = DW_C ? C_q : 8'bz;  // Controlled_Buffer controlled_buffer_19
  assign ALUB = ALU_SEL_C ? C_q : 8'bz;  // Controlled_Buffer controlled_buffer_20
  assign DB = DW_Y ? Y_q : 8'bz;  // Controlled_Buffer controlled_buffer_21
  vis_register Y (.RE(DR_Y), .CLK(CLK), .BUS_IN(DB), .RST(1'b0), .Q(Y_q));
  assign ALUB = ALU_SEL_Y ? Y_q : 8'bz;  // Controlled_Buffer controlled_buffer_22
  assign AB = AW_PC ? PC_q : 16'bz;  // Controlled_Buffer controlled_buffer_23
  assign DB = DW_D ? D_q : 8'bz;  // Controlled_Buffer controlled_buffer_24
  vis_register D (.RE(DR_D), .CLK(CLK), .BUS_IN(DB), .RST(1'b0), .Q(D_q));
  assign ALUB = ALU_SEL_D ? D_q : 8'bz;  // Controlled_Buffer controlled_buffer_25
  assign DB = DW_Z ? Z_q : 8'bz;  // Controlled_Buffer controlled_buffer_26
  vis_register Z (.RE(DR_Z), .CLK(CLK), .BUS_IN(DB), .RST(1'b0), .Q(Z_q));
  assign ALUB = ALU_SEL_Z ? Z_q : 8'bz;  // Controlled_Buffer controlled_buffer_27
  Counter #(.max('h2ff), .width(10)) SP (
    .clr(1'b0), .load(AR_SP), .up(not_2_out), .count(or_5_out), .clk(CLK), .D(AB[9:0]), .Q(SP_q));  // open: carry
  not not_2 (not_2_out, 1'b0);
  or or_5 (or_5_out, 1'b0, 1'b0);
  assign AB = AW_SP ? {{6{1'b1}}, SP_q} : 16'bz;  // Controlled_Buffer controlled_buffer_28

  // Notes on the sheet:
  //   DATA BUS
  //   ADDRESS BUS
endmodule

module dflop (
  input  D,
  input  clk,
  output Q1,
  output Q2
);

  wire and_1_out, and_2_out, not_1_out;

  not not_1 (not_1_out, D);
  and and_1 (and_1_out, not_1_out, clk);
  and and_2 (and_2_out, clk, D);
  nor nor_1 (Q1, and_1_out, Q2);
  nor nor_2 (Q2, Q1, and_2_out);

  // Notes on the sheet:
  //   clk: pull=up
endmodule

module reg1 (
  input  RE,
  input  D,
  input  clk,
  output Q
);

  wire and_1_out, and_2_out, not_1_out, or_1_out;

  not not_1 (not_1_out, RE);
  and and_1 (and_1_out, Q, not_1_out);
  and and_2 (and_2_out, RE, D);
  or or_1 (or_1_out, and_1_out, and_2_out);
  dflop dflop_1 (.D(or_1_out), .clk(clk), .Q1(Q));  // open: Q2
endmodule

module reg8 (
  input  RE,
  input  CLK,
  input  D0,
  input  D1,
  input  D2,
  input  D3,
  input  D4,
  input  D5,
  input  D6,
  input  D7,
  output Q0,
  output Q1,
  output Q2,
  output Q3,
  output Q4,
  output Q5,
  output Q6,
  output Q7
);

  reg1 reg1_1 (.RE(RE), .D(D0), .clk(CLK), .Q(Q0));
  reg1 reg1_2 (.RE(RE), .D(D1), .clk(CLK), .Q(Q1));
  reg1 reg1_3 (.RE(RE), .D(D2), .clk(CLK), .Q(Q2));
  reg1 reg1_4 (.RE(RE), .D(D3), .clk(CLK), .Q(Q3));
  reg1 reg1_5 (.RE(RE), .D(D4), .clk(CLK), .Q(Q4));
  reg1 reg1_6 (.RE(RE), .D(D5), .clk(CLK), .Q(Q5));
  reg1 reg1_7 (.RE(RE), .D(D6), .clk(CLK), .Q(Q6));
  reg1 reg1_8 (.RE(RE), .D(D7), .clk(CLK), .Q(Q7));
endmodule

module reg1ic (
  input  RE,
  input  D,
  input  CLK,
  output Q
);

  wire n7404_1_pin1, n7404_1_pin2, n7404_1_pin9, n7408_1_pin1, n7408_1_pin3, n7408_1_pin5, n7408_1_pin6,
       n7408_1_pin8, n7408_1_pin9, n7408_1_pin11;

  _7408 u_7408_1 (
    .pin1(n7408_1_pin1), .pin2(CLK), .pin3(n7408_1_pin3), .pin4(CLK), .pin5(n7408_1_pin5),
    .pin6(n7408_1_pin6), .pin13(D), .pin12(RE), .pin11(n7408_1_pin11), .pin10(Q), .pin9(n7408_1_pin9),
    .pin8(n7408_1_pin8));
  _7404 u_7404_1 (
    .pin1(n7404_1_pin1), .pin2(n7404_1_pin2), .pin13(RE), .pin12(n7408_1_pin9), .pin11(n7408_1_pin5),
    .pin10(n7408_1_pin1), .pin9(n7404_1_pin9), .pin8(Q));  // open: pin3, pin4, pin5, pin6
  _7432 u_7432_1 (
    .pin1(n7408_1_pin3), .pin2(n7404_1_pin2), .pin3(n7404_1_pin9), .pin4(n7408_1_pin6), .pin5(Q),
    .pin6(n7404_1_pin1), .pin13(n7408_1_pin11), .pin12(n7408_1_pin8), .pin11(n7408_1_pin5));  // open: pin10, pin9, pin8
endmodule

module reg8ic (
  input  RE,
  input  CLK,
  input  D0,
  input  D1,
  input  D2,
  input  D3,
  input  D4,
  input  D5,
  input  D6,
  input  D7,
  output Q0,
  output Q1,
  output Q2,
  output Q3,
  output Q4,
  output Q5,
  output Q6,
  output Q7
);

  reg1ic reg1ic_1 (.RE(RE), .D(D0), .CLK(CLK), .Q(Q0));
  reg1ic reg1ic_2 (.RE(RE), .D(D1), .CLK(CLK), .Q(Q1));
  reg1ic reg1ic_3 (.RE(RE), .D(D2), .CLK(CLK), .Q(Q2));
  reg1ic reg1ic_4 (.RE(RE), .D(D3), .CLK(CLK), .Q(Q3));
  reg1ic reg1ic_5 (.RE(RE), .D(D4), .CLK(CLK), .Q(Q4));
  reg1ic reg1ic_6 (.RE(RE), .D(D5), .CLK(CLK), .Q(Q5));
  reg1ic reg1ic_7 (.RE(RE), .D(D6), .CLK(CLK), .Q(Q6));
  reg1ic reg1ic_8 (.RE(RE), .D(D7), .CLK(CLK), .Q(Q7));
endmodule

module alu (
  input  [7:0] F_in,
  input  [7:0] A,
  input  [7:0] B,
  input  [2:0] OP,
  output [7:0] Q,
  output [7:0] F
);

  wire ad0_p1, ad1_p1, ad2_p1, and_1_out, and_2_out, and_3_out, and_4_out, and_5_out, and_6_out, and_7_out,
       and_8_out, and_9_out, and_10_out, and_11_out, and_12_out, and_13_out, and_14_out, and_15_out,
       and_16_out, and_17_out, and_18_out, and_19_out, and_20_out, and_21_out, and_22_out, and_23_out,
       and_24_out, bd0_p1, bd1_p1, bd2_p1, BF, CF, demultiplexer_2_out0, demultiplexer_2_out1,
       demultiplexer_2_out5, multiplexer_1_out, nor_1_out, nor_2_out, nor_3_out, nor_4_out, nor_5_out,
       nor_6_out, nor_7_out, nor_8_out, not_1_out, not_2_out, not_3_out, OP_ADD, OP_AND, OP_CMP, OP_NOR,
       OP_OR, OP_SUB, or_1_out, or_2_out, or_3_out, or_4_out, or_5_out, or_6_out, or_7_out, or_8_out,
       or_9_out, or_10_out, or_11_out, or_12_out, or_13_out, or_14_out, or_15_out, or_16_out, or_17_out,
       or_18_out, or_19_out, or_20_out, or_21_out, or_22_out, or_23_out, or_24_out, or_25_out, or_26_out,
       or_27_out, qd0_p1, qd1_p1, qd2_p1, xor_1_out, xor_2_out, xor_3_out, xor_4_out, xor_5_out, xor_6_out,
       xor_7_out, xor_8_out, xor_9_out, xor_10_out, xor_11_out, xor_12_out, xor_13_out, xor_14_out,
       xor_15_out, xor_16_out, xor_17_out, xor_18_out, xor_19_out, xor_20_out, xor_21_out, xor_22_out,
       xor_23_out, xor_24_out, xor_25_out, xor_26_out, xor_27_out, xor_28_out, xor_29_out, xor_30_out,
       xor_31_out, xor_32_out;
  wire [7:0] controlled_buffer_1_out, controlled_buffer_2_out;

  Demultiplexer #(.select(3)) demultiplexer_1 (
    .out0(OP_ADD), .out1(OP_SUB), .out2(OP_AND), .out3(OP_OR), .out4(OP_NOR), .out5(OP_CMP), .in(1'b1),
    .sel(OP));  // open: out6, out7
  or or_1 (or_1_out, OP_ADD, or_3_out);
  or or_2 (or_2_out, OP_ADD, or_3_out);
  assign controlled_buffer_1_out = or_2_out ? B : 8'bz;  // Controlled_Buffer controlled_buffer_1
  assign controlled_buffer_2_out = or_1_out ? A : 8'bz;  // Controlled_Buffer controlled_buffer_2
  or or_3 (or_3_out, OP_SUB, OP_CMP);
  Multiplexer multiplexer_1 (.in0(F_in[2]), .in1(not_1_out), .out(multiplexer_1_out), .sel(or_3_out));
  not not_1 (not_1_out, F_in[3]);
  xor xor_1 (xor_1_out, controlled_buffer_1_out[0], or_3_out);
  xor xor_2 (xor_2_out, or_3_out, controlled_buffer_1_out[1]);
  xor xor_3 (xor_3_out, controlled_buffer_1_out[2], or_3_out);
  xor xor_4 (xor_4_out, or_3_out, controlled_buffer_1_out[3]);
  xor xor_5 (xor_5_out, controlled_buffer_1_out[4], or_3_out);
  xor xor_6 (xor_6_out, or_3_out, controlled_buffer_1_out[5]);
  xor xor_7 (xor_7_out, controlled_buffer_1_out[6], or_3_out);
  xor xor_8 (xor_8_out, or_3_out, controlled_buffer_1_out[7]);
  xor xor_9 (xor_9_out, multiplexer_1_out, controlled_buffer_2_out[0]);
  and and_1 (and_1_out, multiplexer_1_out, controlled_buffer_2_out[0]);
  and and_2 (and_2_out, A[0], B[0]);
  and and_3 (and_3_out, A[1], B[1]);
  and and_4 (and_4_out, A[2], B[2]);
  and and_5 (and_5_out, A[3], B[3]);
  and and_6 (and_6_out, A[4], B[4]);
  and and_7 (and_7_out, A[5], B[5]);
  and and_8 (and_8_out, A[6], B[6]);
  and and_9 (and_9_out, A[7], B[7]);
  xor xor_10 (xor_10_out, xor_9_out, xor_1_out);
  and and_10 (and_10_out, xor_1_out, xor_9_out);
  assign Q[0] = OP_AND ? and_2_out : 1'bz;  // Controlled_Buffer controlled_buffer_3
  assign Q[1] = OP_AND ? and_3_out : 1'bz;  // Controlled_Buffer controlled_buffer_4
  assign Q[2] = OP_AND ? and_4_out : 1'bz;  // Controlled_Buffer controlled_buffer_5
  assign Q[3] = OP_AND ? and_5_out : 1'bz;  // Controlled_Buffer controlled_buffer_6
  assign Q[4] = OP_AND ? and_6_out : 1'bz;  // Controlled_Buffer controlled_buffer_7
  assign Q[5] = OP_AND ? and_7_out : 1'bz;  // Controlled_Buffer controlled_buffer_8
  assign Q[6] = OP_AND ? and_8_out : 1'bz;  // Controlled_Buffer controlled_buffer_9
  assign Q[7] = OP_AND ? and_9_out : 1'bz;  // Controlled_Buffer controlled_buffer_10
  or or_4 (or_4_out, OP_SUB, OP_CMP);
  or or_5 (or_5_out, OP_ADD, or_4_out);
  assign Q[0] = or_5_out ? xor_10_out : 1'bz;  // Controlled_Buffer controlled_buffer_11
  xor xor_11 (xor_11_out, and_1_out, and_10_out);
  xor xor_12 (xor_12_out, xor_11_out, controlled_buffer_2_out[1]);
  and and_11 (and_11_out, xor_11_out, controlled_buffer_2_out[1]);
  or or_6 (or_6_out, OP_SUB, OP_CMP);
  or or_7 (or_7_out, OP_ADD, or_6_out);
  xor xor_13 (xor_13_out, xor_12_out, xor_2_out);
  assign Q[1] = or_7_out ? xor_13_out : 1'bz;  // Controlled_Buffer controlled_buffer_12
  and and_12 (and_12_out, xor_2_out, xor_12_out);
  or or_8 (or_8_out, A[0], B[0]);
  assign Q[0] = OP_OR ? or_8_out : 1'bz;  // Controlled_Buffer controlled_buffer_13
  or or_9 (or_9_out, A[1], B[1]);
  assign Q[1] = OP_OR ? or_9_out : 1'bz;  // Controlled_Buffer controlled_buffer_14
  or or_10 (or_10_out, A[2], B[2]);
  assign Q[2] = OP_OR ? or_10_out : 1'bz;  // Controlled_Buffer controlled_buffer_15
  or or_11 (or_11_out, A[3], B[3]);
  assign Q[3] = OP_OR ? or_11_out : 1'bz;  // Controlled_Buffer controlled_buffer_16
  or or_12 (or_12_out, A[4], B[4]);
  assign Q[4] = OP_OR ? or_12_out : 1'bz;  // Controlled_Buffer controlled_buffer_17
  or or_13 (or_13_out, A[5], B[5]);
  assign Q[5] = OP_OR ? or_13_out : 1'bz;  // Controlled_Buffer controlled_buffer_18
  or or_14 (or_14_out, A[6], B[6]);
  assign Q[6] = OP_OR ? or_14_out : 1'bz;  // Controlled_Buffer controlled_buffer_19
  or or_15 (or_15_out, A[7], B[7]);
  assign Q[7] = OP_OR ? or_15_out : 1'bz;  // Controlled_Buffer controlled_buffer_20
  xor xor_14 (xor_14_out, and_11_out, and_12_out);
  xor xor_15 (xor_15_out, xor_14_out, controlled_buffer_2_out[2]);
  and and_13 (and_13_out, xor_14_out, controlled_buffer_2_out[2]);
  xor xor_16 (xor_16_out, xor_15_out, xor_3_out);
  and and_14 (and_14_out, xor_3_out, xor_15_out);
  or or_16 (or_16_out, OP_SUB, OP_CMP);
  or or_17 (or_17_out, OP_ADD, or_16_out);
  assign Q[2] = or_17_out ? xor_16_out : 1'bz;  // Controlled_Buffer controlled_buffer_21
  xor xor_17 (xor_17_out, and_13_out, and_14_out);
  nor nor_1 (nor_1_out, A[0], B[0]);
  assign Q[0] = OP_NOR ? nor_1_out : 1'bz;  // Controlled_Buffer controlled_buffer_22
  nor nor_2 (nor_2_out, A[1], B[1]);
  assign Q[1] = OP_NOR ? nor_2_out : 1'bz;  // Controlled_Buffer controlled_buffer_23
  nor nor_3 (nor_3_out, A[2], B[2]);
  assign Q[2] = OP_NOR ? nor_3_out : 1'bz;  // Controlled_Buffer controlled_buffer_24
  nor nor_4 (nor_4_out, A[3], B[3]);
  assign Q[3] = OP_NOR ? nor_4_out : 1'bz;  // Controlled_Buffer controlled_buffer_25
  nor nor_5 (nor_5_out, A[4], B[4]);
  assign Q[4] = OP_NOR ? nor_5_out : 1'bz;  // Controlled_Buffer controlled_buffer_26
  nor nor_6 (nor_6_out, A[5], B[5]);
  assign Q[5] = OP_NOR ? nor_6_out : 1'bz;  // Controlled_Buffer controlled_buffer_27
  nor nor_7 (nor_7_out, A[6], B[6]);
  assign Q[6] = OP_NOR ? nor_7_out : 1'bz;  // Controlled_Buffer controlled_buffer_28
  nor nor_8 (nor_8_out, A[7], B[7]);
  assign Q[7] = OP_NOR ? nor_8_out : 1'bz;  // Controlled_Buffer controlled_buffer_29
  xor xor_18 (xor_18_out, xor_17_out, controlled_buffer_2_out[3]);
  and and_15 (and_15_out, xor_17_out, controlled_buffer_2_out[3]);
  or or_18 (or_18_out, OP_SUB, OP_CMP);
  or or_19 (or_19_out, OP_ADD, or_18_out);
  xor xor_19 (xor_19_out, xor_18_out, xor_4_out);
  assign Q[3] = or_19_out ? xor_19_out : 1'bz;  // Controlled_Buffer controlled_buffer_30
  and and_16 (and_16_out, xor_4_out, xor_18_out);
  xor xor_20 (xor_20_out, and_15_out, and_16_out);
  xor xor_21 (xor_21_out, xor_20_out, controlled_buffer_2_out[4]);
  and and_17 (and_17_out, xor_20_out, controlled_buffer_2_out[4]);
  xor xor_22 (xor_22_out, xor_21_out, xor_5_out);
  and and_18 (and_18_out, xor_5_out, xor_21_out);
  or or_20 (or_20_out, OP_SUB, OP_CMP);
  or or_21 (or_21_out, OP_ADD, or_20_out);
  assign Q[4] = or_21_out ? xor_22_out : 1'bz;  // Controlled_Buffer controlled_buffer_31
  xor xor_23 (xor_23_out, and_17_out, and_18_out);
  xor xor_24 (xor_24_out, xor_23_out, controlled_buffer_2_out[5]);
  and and_19 (and_19_out, xor_23_out, controlled_buffer_2_out[5]);
  or or_22 (or_22_out, OP_SUB, OP_CMP);
  or or_23 (or_23_out, OP_ADD, or_22_out);
  xor xor_25 (xor_25_out, xor_24_out, xor_6_out);
  assign Q[5] = or_23_out ? xor_25_out : 1'bz;  // Controlled_Buffer controlled_buffer_32
  and and_20 (and_20_out, xor_6_out, xor_24_out);
  xor xor_26 (xor_26_out, and_19_out, and_20_out);
  xor xor_27 (xor_27_out, xor_26_out, controlled_buffer_2_out[6]);
  and and_21 (and_21_out, xor_26_out, controlled_buffer_2_out[6]);
  xor xor_28 (xor_28_out, xor_27_out, xor_7_out);
  and and_22 (and_22_out, xor_7_out, xor_27_out);
  Demultiplexer #(.select(3)) demultiplexer_2 (
    .out0(demultiplexer_2_out0), .out1(demultiplexer_2_out1), .out5(demultiplexer_2_out5), .in(1'b1), .sel(OP));  // open: out2, out3, out4, out6, out7
  or or_24 (or_24_out, OP_SUB, OP_CMP);
  or or_25 (or_25_out, OP_ADD, or_24_out);
  assign Q[6] = or_25_out ? xor_28_out : 1'bz;  // Controlled_Buffer controlled_buffer_33
  xor xor_29 (xor_29_out, and_21_out, and_22_out);
  xor xor_30 (xor_30_out, xor_29_out, controlled_buffer_2_out[7]);
  and and_23 (and_23_out, xor_29_out, controlled_buffer_2_out[7]);
  or or_26 (or_26_out, OP_SUB, OP_CMP);
  or or_27 (or_27_out, OP_ADD, or_26_out);
  xor xor_31 (xor_31_out, xor_30_out, xor_8_out);
  assign Q[7] = or_27_out ? xor_31_out : 1'bz;  // Controlled_Buffer controlled_buffer_34
  and and_24 (and_24_out, xor_8_out, xor_30_out);
  Multiplexer multiplexer_2 (.in0(F_in[0]), .in1(F[4]), .out(F[0]), .sel(demultiplexer_2_out5));
  Multiplexer multiplexer_3 (.in0(F_in[1]), .in1(BF), .out(F[1]), .sel(demultiplexer_2_out5));
  Multiplexer multiplexer_4 (.in0(F_in[2]), .in1(CF), .out(F[2]), .sel(demultiplexer_2_out0));
  Multiplexer multiplexer_5 (.in0(F_in[3]), .in1(BF), .out(F[3]), .sel(demultiplexer_2_out1));
  xor xor_32 (xor_32_out, and_23_out, and_24_out);
  LED LF (.in(F[1]));
  LED u_CF (.in(F[2]));
  LED u_BF (.in(F[3]));
  LED ZF (.in(F[4]));
  not not_2 (not_2_out, or_3_out);
  LED EF (.in(F[0]));
  and and_25 (CF, not_2_out, xor_32_out);
  not not_3 (not_3_out, xor_32_out);
  and and_26 (BF, or_3_out, not_3_out);
  nor nor_9 (F[4], Q[0], Q[1], Q[2], Q[3], Q[4], Q[5], Q[6], Q[7]);
  // _7_Segment_Display qd2: pin names not known; wires that end beside it: qd2_p1, qd2_p1
  // BCD_to_7_Segment_decoder bcd_to_7_segment_decoder_1: pin names not known
  // Binary_to_BCD_converter #(.binvalue(8)) binary_to_bcd_converter_1: pin names not known; wires that end beside it: Q
  // _7_Segment_Display qd1: pin names not known; wires that end beside it: qd1_p1, qd1_p1
  // _7_Segment_Display qd0: pin names not known; wires that end beside it: qd0_p1, qd0_p1
  // BCD_to_7_Segment_decoder bcd_to_7_segment_decoder_2: pin names not known
  // BCD_to_7_Segment_decoder bcd_to_7_segment_decoder_3: pin names not known
  // _7_Segment_Display ad2: pin names not known; wires that end beside it: ad2_p1, ad2_p1
  // BCD_to_7_Segment_decoder bcd_to_7_segment_decoder_4: pin names not known
  // _7_Segment_Display bd2: pin names not known; wires that end beside it: bd2_p1, bd2_p1
  // BCD_to_7_Segment_decoder bcd_to_7_segment_decoder_5: pin names not known
  // _7_Segment_Display ad1: pin names not known; wires that end beside it: ad1_p1, ad1_p1
  // BCD_to_7_Segment_decoder bcd_to_7_segment_decoder_6: pin names not known
  // Binary_to_BCD_converter #(.binvalue(8)) binary_to_bcd_converter_2: pin names not known; wires that end beside it: A
  // _7_Segment_Display bd1: pin names not known; wires that end beside it: bd1_p1, bd1_p1
  // BCD_to_7_Segment_decoder bcd_to_7_segment_decoder_7: pin names not known
  // Binary_to_BCD_converter #(.binvalue(8)) binary_to_bcd_converter_3: pin names not known; wires that end beside it: B
  // _7_Segment_Display ad0: pin names not known; wires that end beside it: ad0_p1, ad0_p1
  // BCD_to_7_Segment_decoder bcd_to_7_segment_decoder_8: pin names not known
  // _7_Segment_Display bd0: pin names not known; wires that end beside it: bd0_p1, bd0_p1
  // BCD_to_7_Segment_decoder bcd_to_7_segment_decoder_9: pin names not known

  assign F[7:5] = 3'b000;

  // Other names for the same wires on the sheet: ZF = F[4]; F_t[7:0] = F_in
endmodule

module bitadd (
  input  C_in,
  input  A,
  input  B,
  output Q,
  output C_out
);

  wire and_1_out, and_2_out, xor_1_out;

  xor xor_1 (xor_1_out, A, C_in);
  and and_1 (and_1_out, C_in, A);
  xor xor_2 (Q, xor_1_out, B);
  and and_2 (and_2_out, B, xor_1_out);
  xor xor_3 (C_out, and_1_out, and_2_out);
endmodule

module mem (
  input  [15:0] ADDR,
  input  WE,
  input  CLK,
  input  [7:0] D_in,
  output [7:0] D_Out
);

  wire [7:0] ram_1_dout, rom_1_data;

  RAM #(.addrWidth(15), .enables("line")) ram_1 (.addr(ADDR[14:0]), .we(WE), .clk(CLK), .din(D_in), .dout(ram_1_dout));
  ROM #(.addrWidth(15)) rom_1 (.addr(ADDR[14:0]), .data(rom_1_data));
  Multiplexer #(.width(8)) multiplexer_1 (.in0(rom_1_data), .in1(ram_1_dout), .out(D_Out), .sel(ADDR[15]));

  // Notes on the sheet:
  //   contents of rom_1 (hex, n*v repeats v):
  //   2 ff ff
endmodule

module vis_register (
  input  [7:0] BUS_IN,
  input  RE,
  input  CLK,
  input  RST,
  output [7:0] Q
);

  wire n7_segment_display_1_p1, n7_segment_display_2_p1, n7_segment_display_3_p1;

  Register register_1 (.D(BUS_IN), .en(RE), .clk(CLK), .Q(Q), .clr(RST));
  // _7_Segment_Display 7_segment_display_1: pin names not known; wires that end beside it: n7_segment_display_1_p1, n7_segment_display_1_p1
  // BCD_to_7_Segment_decoder bcd_to_7_segment_decoder_1: pin names not known
  // Binary_to_BCD_converter #(.binvalue(8)) binary_to_bcd_converter_1: pin names not known; wires that end beside it: Q
  // _7_Segment_Display 7_segment_display_2: pin names not known; wires that end beside it: n7_segment_display_2_p1, n7_segment_display_2_p1
  // _7_Segment_Display 7_segment_display_3: pin names not known; wires that end beside it: n7_segment_display_3_p1, n7_segment_display_3_p1
  // BCD_to_7_Segment_decoder bcd_to_7_segment_decoder_2: pin names not known
  // BCD_to_7_Segment_decoder bcd_to_7_segment_decoder_3: pin names not known
endmodule
